// Logisim project p3.circ as structural Verilog: 1 circuit, main circuit main
module main (
  input  in_1,
  input  in_2
);

  wire CLCK, CTRLW, decoder_1_out0, decoder_1_out1, decoder_1_out2, decoder_1_out3, decoder_1_out4,
       decoder_1_out5, decoder_1_out6, decoder_1_out7;
  wire [2:0] and_1_out, and_2_out, bit_extender_1_out, not_1_out, SEL, SELB, SELD, SELR;
  wire [7:0] adder_1_out, register_1_q;
  wire [11:0] ALU;
  wire [15:0] A, ADD, adder_5_out, and_3_out, and_4_out, and_5_out, AUR, B, bit_extender_3_out,
       bit_extender_4_out, C, D, DOTS, INSRT, LIR, multiplier_1_out, multiplier_2_out, not_2_out, R0_q, R1_q,
       R2_q, R3_q, R4_q, R5_q, R6_q, R7_q, RD;

  Register register_1 (.D(adder_1_out), .en(1'b1), .clk(CLCK), .Q(register_1_q), .clr(in_1));
  Clock clock_1 (.out(CLCK));
  // Probe on register_1_q
  ROM #(.dataWidth(16)) rom_1 (.addr(register_1_q), .data({ALU, SELR, CTRLW}));
  Adder adder_1 (.a(register_1_q), .b(8'h1), .out(adder_1_out));  // open: cin, cout
  // Probe on adder_1_out
  // Probe on SELR
  Decoder #(.enable("false"), .select(3)) decoder_1 (
    .out0(decoder_1_out0), .out1(decoder_1_out1), .out2(decoder_1_out2), .out3(decoder_1_out3),
    .out4(decoder_1_out4), .out5(decoder_1_out5), .out6(decoder_1_out6), .out7(decoder_1_out7), .sel(SELR));
  Register #(.width(16)) R7 (.D(INSRT), .en(decoder_1_out7), .clk(CLCK), .Q(R7_q), .clr(in_1));
  Register #(.width(16)) R6 (.D(INSRT), .en(decoder_1_out6), .clk(CLCK), .Q(R6_q), .clr(in_1));
  Register #(.width(16)) R5 (.D(INSRT), .en(decoder_1_out5), .clk(CLCK), .Q(R5_q), .clr(in_1));
  Register #(.width(16)) R4 (.D(INSRT), .en(decoder_1_out4), .clk(CLCK), .Q(R4_q), .clr(in_1));
  Multiplexer #(.width(16)) multiplexer_1 (.in0(LIR), .in1(AUR), .out(INSRT), .sel(CTRLW));
  Multiplexer #(.select(3), .width(16)) multiplexer_2 (
    .in0(R0_q), .in1(R1_q), .in2(R2_q), .in3(R3_q), .in4(R4_q), .in5(R5_q), .in6(R6_q), .in7(R7_q), .out(RD),
    .sel(SELR));
  // Probe on INSRT
  Register #(.width(16)) R3 (.D(INSRT), .en(decoder_1_out3), .clk(CLCK), .Q(R3_q), .clr(in_1));
  Register #(.width(16)) R2 (.D(INSRT), .en(decoder_1_out2), .clk(CLCK), .Q(R2_q), .clr(in_1));
  Multiplexer #(.select(3), .width(16)) multiplexer_3 (
    .in0(R0_q), .in1(R1_q), .in2(R2_q), .in3(R3_q), .in4(R4_q), .in5(R5_q), .in6(R6_q), .in7(R7_q), .out(A),
    .sel(ALU[5:3]));
  Register #(.width(16)) R1 (.D(INSRT), .en(decoder_1_out1), .clk(CLCK), .Q(R1_q), .clr(in_1));
  Multiplexer #(.select(3), .width(16)) multiplexer_4 (
    .in0(R0_q), .in1(R1_q), .in2(R2_q), .in3(R3_q), .in4(R4_q), .in5(R5_q), .in6(R6_q), .in7(R7_q), .out(B),
    .sel(SELB));
  Register #(.width(16)) R0 (.D(INSRT), .en(decoder_1_out0), .clk(CLCK), .Q(R0_q), .clr(in_1));
  Multiplexer #(.select(3), .width(16)) multiplexer_5 (
    .in0(R0_q), .in1(R1_q), .in2(R2_q), .in3(R3_q), .in4(R4_q), .in5(R5_q), .in6(R6_q), .in7(R7_q), .out(C),
    .sel(ALU[8:6]));
  Multiplexer #(.select(3), .width(16)) multiplexer_6 (
    .in0(R0_q), .in1(R1_q), .in2(R2_q), .in3(R3_q), .in4(R4_q), .in5(R5_q), .in6(R6_q), .in7(R7_q), .out(D),
    .sel(SELD));
  assign bit_extender_1_out = {{2{ALU[1]}}, ALU[1]};  // Bit_Extender bit_extender_1
  assign and_1_out = SELR & bit_extender_1_out;  // AND_Gate and_1, 3 bits wide
  // Probe on SEL
  assign not_1_out = ~bit_extender_1_out;  // NOT_Gate not_1, 3 bits wide
  assign SEL = and_1_out ^ and_2_out;  // XOR_Gate xor_1, 3 bits wide
  assign LIR = {{4{ALU[11]}}, ALU};  // Bit_Extender bit_extender_2
  // Probe on ALU[5:3]
  assign and_2_out = not_1_out & ALU[8:6];  // AND_Gate and_2, 3 bits wide
  // Probe on ALU[8:6]
  assign bit_extender_3_out = {{15{ALU[0]}}, ALU[0]};  // Bit_Extender bit_extender_3
  assign and_3_out = ADD & bit_extender_3_out;  // AND_Gate and_3, 16 bits wide
  assign AUR = and_3_out ^ and_4_out;  // XOR_Gate xor_2, 16 bits wide
  // Probe on AUR
  assign not_2_out = ~bit_extender_3_out;  // NOT_Gate not_2, 16 bits wide
  assign and_4_out = not_2_out & DOTS;  // AND_Gate and_4, 16 bits wide
  // Probe on C
  // Probe on A
  Adder #(.width(16)) adder_2 (.a(C), .b(A), .out(ADD), .cin(in_2));  // open: cout
  assign bit_extender_4_out = {{15{ALU[2]}}, ALU[2]};  // Bit_Extender bit_extender_4
  Adder #(.width(3)) adder_3 (.a(ALU[5:3]), .b(3'b001), .out(SELB));  // open: cin, cout
  Adder #(.width(3)) adder_4 (.a(SEL), .b(3'b001), .out(SELD));  // open: cin, cout
  // Probe on ADD
  assign and_5_out = RD & bit_extender_4_out;  // AND_Gate and_5, 16 bits wide
  Multiplier #(.width(16)) multiplier_1 (.a(A), .b(C), .out(multiplier_1_out));  // open: cin, cout
  Multiplier #(.mode("twosComplement"), .width(16)) multiplier_2 (
    .a(B), .b(D), .out(multiplier_2_out));  // open: cin, cout
  Adder #(.width(16)) adder_5 (.a(multiplier_1_out), .b(multiplier_2_out), .out(adder_5_out));  // open: cin, cout
  // Probe on DOTS
  Adder #(.width(16)) adder_6 (.a(and_5_out), .b(adder_5_out), .out(DOTS));  // open: cin, cout

  // Other names for the same wires on the sheet: AU[11:0] = ALU; FUNC3[1:0] = ALU[1:0]; LI[11:0] = ALU;
  //   SELA[2:0] = ALU[5:3]; SELC[2:0] = ALU[8:6]; SELRD[2:0] = SELR

  // Notes on the sheet:
  //   contents of rom_1 (hex, n*v repeats v):
  //   20 32 44 26 18 5a 2c 2e c97 121 1341
endmodule
