// Logisim project projeto3.circ as structural Verilog: 1 circuit, main circuit main
module main (
  input  in_1,
  input  in_2
);

  wire ADD_INST, CLCK, decoder_1_out0, decoder_1_out1, decoder_1_out2, decoder_1_out3, decoder_1_out4,
       decoder_1_out5, decoder_1_out6, decoder_1_out7, LI_INST;
  wire [2:0] SELR;
  wire [7:0] adder_1_out, PC_q;
  wire [11:1] ALU;
  wire [15:0] A, ADD, adder_3_out, and_1_out, B, bit_extender_1_out, bit_extender_2_out, C, D, DOTS, INSRT,
       multiplexer_6_out, multiplier_1_out, multiplier_2_out, R0, R1, R2, R3, R4, R5, R6, R7, RD;

  Clock clock_1 (.out(CLCK));
  Register PC (.D(adder_1_out), .en(1'b1), .clk(CLCK), .Q(PC_q), .clr(in_1));
  // Probe on PC_q
  ROM #(.dataWidth(16)) rom_1 (.addr(PC_q), .data({ALU, ADD_INST, SELR, LI_INST}));
  Adder adder_1 (.a(PC_q), .b(8'h1), .out(adder_1_out));  // open: cin, cout
  // Probe on adder_1_out
  // Probe on SELR
  Decoder #(.enable("false"), .select(3)) decoder_1 (
    .out0(decoder_1_out0), .out1(decoder_1_out1), .out2(decoder_1_out2), .out3(decoder_1_out3),
    .out4(decoder_1_out4), .out5(decoder_1_out5), .out6(decoder_1_out6), .out7(decoder_1_out7), .sel(SELR));
  // Probe on SELR
  Register #(.width(16)) u_R7 (.D(INSRT), .en(decoder_1_out7), .clk(CLCK), .Q(R7), .clr(in_1));
  Register #(.width(16)) u_R6 (.D(INSRT), .en(decoder_1_out6), .clk(CLCK), .Q(R6), .clr(in_1));
  Register #(.width(16)) u_R5 (.D(INSRT), .en(decoder_1_out5), .clk(CLCK), .Q(R5), .clr(in_1));
  // Probe on {ALU, ADD_INST}
  Register #(.width(16)) u_R4 (.D(INSRT), .en(decoder_1_out4), .clk(CLCK), .Q(R4), .clr(in_1));
  Multiplexer #(.select(3), .width(16)) multiplexer_1 (
    .in0(R0), .in1(R1), .in2(R2), .in3(R3), .in4(R4), .in5(R5), .in6(R6), .in7(R7), .out(RD), .sel(SELR));
  // Probe on ALU[5:3]
  // Probe on ALU[8:6]
  Register #(.width(16)) u_R3 (.D(INSRT), .en(decoder_1_out3), .clk(CLCK), .Q(R3), .clr(in_1));
  Multiplexer #(.select(3), .width(16)) multiplexer_2 (
    .in0(R0), .in1(R1), .in2(R2), .in3(R3), .in4(R4), .in5(R5), .in6(R6), .in7(R7), .out(A), .sel(ALU[5:3]));
  Register #(.width(16)) u_R2 (.D(INSRT), .en(decoder_1_out2), .clk(CLCK), .Q(R2), .clr(in_1));
  Multiplexer #(.select(3), .width(16)) multiplexer_3 (
    .in0(R1), .in1(R2), .in2(R3), .in3(R4), .in4(R5), .in5(R6), .in6(R7), .in7(R0), .out(B), .sel(ALU[5:3]));
  Register #(.width(16)) u_R1 (.D(INSRT), .en(decoder_1_out1), .clk(CLCK), .Q(R1), .clr(in_1));
  // Probe on C
  // Probe on A
  Register #(.width(16)) u_R0 (.D(INSRT), .en(decoder_1_out0), .clk(CLCK), .Q(R0), .clr(in_1));
  Multiplexer #(.select(3), .width(16)) multiplexer_4 (
    .in0(R0), .in1(R1), .in2(R2), .in3(R3), .in4(R4), .in5(R5), .in6(R6), .in7(R7), .out(C), .sel(ALU[8:6]));
  // Probe on ADD
  Adder #(.width(16)) adder_2 (.a(C), .b(A), .out(ADD), .cin(in_2));  // open: cout
  Multiplexer #(.select(3), .width(16)) multiplexer_5 (
    .in0(R1), .in1(R2), .in2(R3), .in3(R4), .in4(R5), .in5(R6), .in6(R7), .in7(R0), .out(D), .sel(ALU[8:6]));
  // Probe on ALU[2]
  assign bit_extender_1_out = {{15{ALU[2]}}, ALU[2]};  // Bit_Extender bit_extender_1
  Multiplier #(.width(16)) multiplier_1 (.a(A), .b(C), .out(multiplier_1_out));  // open: cin, cout
  Multiplier #(.mode("twosComplement"), .width(16)) multiplier_2 (
    .a(B), .b(D), .out(multiplier_2_out));  // open: cin, cout
  assign and_1_out = bit_extender_1_out & RD;  // AND_Gate and_1, 16 bits wide
  Adder #(.width(16)) adder_3 (.a(multiplier_1_out), .b(multiplier_2_out), .out(adder_3_out));  // open: cin, cout
  // Probe on DOTS
  Adder #(.width(16)) adder_4 (.a(and_1_out), .b(adder_3_out), .out(DOTS));  // open: cin, cout
  Multiplexer #(.width(16)) multiplexer_6 (.in0(DOTS), .in1(ADD), .out(multiplexer_6_out), .sel(ADD_INST));
  assign bit_extender_2_out = {{4{ALU[11]}}, {ALU, ADD_INST}};  // Bit_Extender bit_extender_2
  // Probe on INSRT
  Multiplexer #(.width(16)) multiplexer_7 (
    .in0(multiplexer_6_out), .in1(bit_extender_2_out), .out(INSRT), .sel(LI_INST));

  // Other names for the same wires on the sheet: ALU[0] = ADD_INST; LI[11:0] = {ALU, ADD_INST}; DOT_INST = ALU[1];
  //   DOTA_INST = ALU[2]; SELA[2:0] = ALU[5:3]; SELB[2:0] = ALU[5:3]; SELC[2:0] = ALU[8:6]; SELD[2:0] = ALU[8:6];
  //   SELRD[2:0] = SELR

  // Notes on the sheet:
  //   contents of rom_1 (hex, n*v repeats v):
  //   12c1 12d3 12c5 12d7 240
endmodule
